// Logisim project exercicio03_arqcomp.circ as structural Verilog: 1 circuit, main circuit main
module main (
  input  A,
  input  B,
  input  in_3,
  input  C,
  input  D
);

  wire and_1_out, and_2_out, or_1_out;

  and and_1 (and_1_out, A, B);
  and and_2 (and_2_out, C, D);
  or or_1 (or_1_out, and_1_out, and_2_out);
endmodule
