// Logisim project exercicio02_arqcomp.circ as structural Verilog: 1 circuit, main circuit main
module main (
  input  A,
  input  C,
  input  B,
  input  in_4,
  input  D,
  input  E,
  input  F
);

  wire and_1_out, and_2_out, or_1_out, or_2_out;

  and and_1 (and_1_out, A, C);
  or or_1 (or_1_out, B, D);
  and and_2 (and_2_out, E, F);
  or or_2 (or_2_out, and_1_out, or_1_out, and_2_out);
endmodule
