// Logisim project exercicio05_arqcomp.circ as structural Verilog: 1 circuit, main circuit main
module main (
  input  A,
  input  B,
  input  D,
  input  in_4,
  input  C,
  input  E,
  input  F
);

  wire and_1_out, or_1_out, or_2_out;

  or or_1 (or_1_out, B, D);
  and and_1 (and_1_out, E, F);
  or or_2 (or_2_out, A, or_1_out, C, and_1_out);
endmodule
