// Logisim project exercicio06_arqcomp.circ as structural Verilog: 1 circuit, main circuit main
module main (
  input  A,
  input  B,
  input  in_3,
  input  C,
  input  D
);

  wire or_1_out, or_2_out;

  or or_1 (or_1_out, A, B, C);
  or or_2 (or_2_out, or_1_out, D);
endmodule
