// Logisim project primeiro.circ as structural Verilog: 1 circuit, main circuit main
module main (
  input  A,
  input  B,
  input  C,
  input  A_2,
  input  B_2,
  input  in_6,
  input  C_2,
  input  A_3,
  input  B_3,
  input  C_3
);

  wire and_1_out, and_2_out, and_3_out, not_1_out, not_2_out, not_3_out, not_4_out, not_5_out, or_1_out;

  not not_1 (not_1_out, A);
  not not_2 (not_2_out, B);
  not not_3 (not_3_out, C);
  not not_4 (not_4_out, A_2);
  not not_5 (not_5_out, C_3);
  and and_1 (and_1_out, not_1_out, not_2_out, not_3_out);
  and and_2 (and_2_out, not_4_out, B_2, C_2);
  and and_3 (and_3_out, A_3, B_3, not_5_out);
  or or_1 (or_1_out, and_1_out, and_2_out, and_3_out);
endmodule
