// Logisim project exercicio02_arqcomp.circ as structural Verilog: 1 circuit, main circuit main
module main (
  input  in_1,
  input  in_2,
  input  in_3,
  input  in_4,
  input  in_5
);

  wire and_1_out, or_1_out, or_2_out;

  and and_1 (and_1_out, in_1, in_2);
  or or_1 (or_1_out, in_4, in_5);
  or or_2 (or_2_out, and_1_out, or_1_out);
endmodule
